# Fritzing sketch wiring-diagram (saved by Fritzing 1.0.4)
breadboards: 1

parts:
  Part1 = Adafruit T-Cobbler Plus [part_number="Adafruit #1989 and #2028"]
  Part2 = BME280 Breakout  # not connected
  Part3 = BME280 Breakout  # not connected

nets:
  N1: Part1.GPIO27, Part1.GPIO22
  N2: Part1.GPIO26, Part1.GPIO16
  N3: Part1.GPIO18, Part1.GPIO23
  N4: Part1.GPIO24, Part1.GPIO25

custom parts:
  Adafruit T-Cobbler Plus: The Raspberry Pi has landed on the Maker World like a 40-GPIO pinned, quad-USB ported, credit card sized bomb of DIY joy. And while you can use most of our great Model B accessories by hooking up our downgrade cable, its probably a good time to upgrade your set up and accessorize using all of the 40 pins. That's why we now carry the Assembled Adafruit Pi T-Cobbler Plus - Breakout + Cable for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
